# Fritzing sketch DigitalIinputTest (saved by Fritzing 0.9.5d)
breadboards: 1

parts:
  U1 = ESP32-38PinWide [part_number=ESP32-38PinWide]
  S1 = Pushbutton [package="[SMD]"]
  S2 = Pushbutton [package="[THT]"]
  S3 = Pushbutton [package="[THT]"]
  S4 = Pushbutton [package="[THT]"]
  LED1 = LED - 5mm [color="Red (633nm)" package="5 mm [THT]"]
  LED7 = LED - 5mm [color="Red (633nm)" package="5 mm [THT]"]
  LED8 = LED - 5mm [color="Red (633nm)" package="5 mm [THT]"]
  LED9 = LED - 5mm [color="Red (633nm)" package="5 mm [THT]"]
  R1 = Resistor [tolerance=±5% resistance=330 package=THT]
  R2 = Resistor [tolerance=±5% resistance=330 package=THT]  # not connected
  R3 = Resistor [tolerance=±5% resistance=330 package=THT]
  R4 = Resistor [tolerance=±5% resistance=330 package=THT]
  R5 = Resistor [tolerance=±5% resistance=330 package=THT]

nets:
  N1: U1.3.3, S1.Pin_1, S1.Pin_2, S2.Pin_1, S2.Pin_2, S3.Pin_1, S3.Pin_2, S4.Pin_1, S4.Pin_2
  N2: U1.GPIO36, S4.Pin_3, S4.Pin_4, LED9.anode
  N3: U1.GPIO39, S3.Pin_3, S3.Pin_4, LED8.anode
  N4: U1.GPIO34, S2.Pin_3, S2.Pin_4, LED7.anode
  N5: U1.GPIO35, S1.Pin_3, S1.Pin_4, LED1.anode
  N6: U1.VIN, R1.Pin_0, R3.Pin_0, R4.Pin_0
  N7: LED1.cathode, R1.Pin_1
  N8: LED7.cathode, R3.Pin_1
  N9: LED8.cathode, R4.Pin_1
  N10: LED9.cathode, R5.Pin_1

custom parts:
  ESP32-38PinWide: Generic 38-Pin ESP32 with wide format (only access to one side of pins on a breadboard) based on Stephen Lilley's HiLetgo ESP-WROOM-32 ESP32 ESP-32S Development Board.
