# Fritzing sketch whitepaperdisplay (saved by Fritzing 0.9.5d)
breadboards: 1

parts:
  U2 = ESP32-38PinWide [part_number=ESP32-38PinWide]
  Part10 = Adafruit 2.9" eInk Display Breakout [part_number="Adafruit #1028"]

nets:
  N1: U2.3.3, Part10.3.3V
  GND: U2.GND, Part10.GND
  VIN: U2.VIN, Part10.VIN
  N2: U2.GPIO16, Part10.DC
  N3: U2.GPIO17, Part10.SDCS
  N4: U2.GPIO5, Part10.RESET
  N5: U2.GPIO18, Part10.SCLK
  N6: U2.GPIO19, Part10.BUSY
  N7: U2.GPIO23, Part10.MOSI

custom parts:
  ESP32-38PinWide: Generic 38-Pin ESP32 with wide format (only access to one side of pins on a breadboard) based on Stephen Lilley's HiLetgo ESP-WROOM-32 ESP32 ESP-32S Development Board.
  Adafruit 2.9" eInk Display Breakout: Easy e-paper finally comes to microcontrollers, with this breakout that's designed to make it a breeze to add a tri-color eInk display. Chances are you've seen one of those new-fangled 'e-readers' like the Kindle or Nook. They have gigantic electronic paper 'static' displays - that means the image stays on the display even when power is completely disconnected. The image is also high contrast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
