# Fritzing sketch spider (saved by Fritzing 0.9.5d)
breadboards: 3

parts:
  U2 = ESP32-38PinWide [part_number=ESP32-38PinWide]
  MOTOR4 = 28BYJ-48 Stepper Motor
  X5 = X113647 Stepper Driver Board [part_number=X113647 package=board]
  MOTOR5 = 28BYJ-48 Stepper Motor
  X6 = X113647 Stepper Driver Board [part_number=X113647 package=board]
  Part1 = 16-Channel 12-bit PCA9685 PWM/Servo Driver
  Part2 = 16-Channel 12-bit PCA9685 PWM/Servo Driver
  Part3 = 16-Channel 12-bit PCA9685 PWM/Servo Driver
  TP1 = TP4056 [chip_label=TP4056 package="DIP (Dual Inline) [THT]"]
  Part4 = Lithium Ion Polymer Battery 3.7v 500mAh [part_number=1578]
  D1 = SOLAR-IXYS [package=solarbit-12x1]
  SERVO1 = Tower Pro SG90 servo [part_number=101246]
  SERVO5 = Tower Pro SG90 servo [part_number=101246]
  SERVO6 = Tower Pro SG90 servo [part_number=101246]
  SERVO7 = Tower Pro SG90 servo [part_number=101246]
  SERVO8 = Tower Pro SG90 servo [part_number=101246]
  SERVO9 = Tower Pro SG90 servo [part_number=101246]
  SERVO10 = Tower Pro SG90 servo [part_number=101246]
  SERVO11 = Tower Pro SG90 servo [part_number=101246]
  SERVO12 = Tower Pro SG90 servo [part_number=101246]
  SERVO13 = Tower Pro SG90 servo [part_number=101246]
  SERVO14 = Tower Pro SG90 servo [part_number=101246]
  SERVO15 = Tower Pro SG90 servo [part_number=101246]
  SERVO16 = Tower Pro SG90 servo [part_number=101246]
  SERVO17 = Tower Pro SG90 servo [part_number=101246]
  SERVO18 = Tower Pro SG90 servo [part_number=101246]
  SERVO19 = Tower Pro SG90 servo [part_number=101246]
  SERVO20 = Tower Pro SG90 servo [part_number=101246]
  SERVO21 = Tower Pro SG90 servo [part_number=101246]
  SERVO22 = Tower Pro SG90 servo [part_number=101246]
  SERVO23 = Tower Pro SG90 servo [part_number=101246]
  SERVO24 = Tower Pro SG90 servo [part_number=101246]
  SERVO25 = Tower Pro SG90 servo [part_number=101246]
  SERVO26 = Tower Pro SG90 servo [part_number=101246]
  SERVO27 = Tower Pro SG90 servo [part_number=101246]
  SERVO28 = Tower Pro SG90 servo [part_number=101246]
  Part5 = 16-Channel 12-bit PCA9685 PWM/Servo Driver
  SERVO29 = Tower Pro SG90 servo [part_number=101246]
  SERVO30 = Tower Pro SG90 servo [part_number=101246]
  SERVO31 = Tower Pro SG90 servo [part_number=101246]
  SERVO32 = Tower Pro SG90 servo [part_number=101246]
  SERVO33 = Tower Pro SG90 servo [part_number=101246]
  SERVO34 = Tower Pro SG90 servo [part_number=101246]
  SERVO35 = Tower Pro SG90 servo [part_number=101246]
  SERVO36 = Tower Pro SG90 servo [part_number=101246]
  HC-SR04_Sensor_1 = HC-SR04 Ultrasonic Distance Sensor
  Part6 = OLED Monochrome 128x64 0.96 inch [part_number=326]
  Part7 = InvenSense MPU6050
  ESP32_-_Back1 = ESP32 - CAM
  ESP32_-_Back2 = ESP32 - CAM
  U3 = SWITCH_SPDT [package=kps-1290]
  Part8 = NeoPixel Jewel [part_number=2226]
  Part9 = NeoPixel Jewel [part_number=2226]
  R1 = Resistor [tolerance=±5% resistance=10k package=THT]
  R2 = Resistor [tolerance=±5% resistance=10k package=THT]
  R3 = Resistor [tolerance=±5% resistance=10k package=THT]
  R4 = Resistor [tolerance=±5% resistance=10k package=THT]
  R5 = Resistor [tolerance=±5% resistance=10k package=THT]
  R6 = Resistor [tolerance=±5% resistance=10k package=THT]
  R7 = Resistor [tolerance=±5% resistance=10k package=THT]
  R8 = Resistor [tolerance=±5% resistance=10k package=THT]
  S1 = Momentary Switch [package=ksa_sealed_tac_switch]
  S2 = Momentary Switch [package=ksa_sealed_tac_switch]
  S3 = Momentary Switch [package=ksa_sealed_tac_switch]
  S4 = Momentary Switch [package=ksa_sealed_tac_switch]
  S5 = Momentary Switch [package=ksa_sealed_tac_switch]
  S6 = Momentary Switch [package=ksa_sealed_tac_switch]
  S7 = Momentary Switch [package=ksa_sealed_tac_switch]
  S8 = Momentary Switch [package=ksa_sealed_tac_switch]
  R9 = Resistor [tolerance=±5% resistance=100k package=THT]
  R11 = Resistor [tolerance=±5% resistance=100k package=THT]
  J1 = Piezo Speaker
  Part11 = Waveshare 2.9" eInk Display Breakout  # not connected
  R12 = Resistor [tolerance=±5% resistance=10k package=THT]
  S9 = Momentary Switch [package=ksa_sealed_tac_switch]
  S10 = Momentary Switch [package=ksa_sealed_tac_switch]
  S11 = Momentary Switch [package=ksa_sealed_tac_switch]
  S12 = Momentary Switch [package=ksa_sealed_tac_switch]
  R13 = Resistor [tolerance=±5% resistance=10k package=THT]
  R14 = Resistor [tolerance=±5% resistance=10k package=THT]
  R15 = Resistor [tolerance=±5% resistance=10k package=THT]

nets:
  VCC: U2.3.3, Part1.VCC, Part2.VCC, Part2.A0, Part3.VCC, Part3.A1, Part5.VCC, HC-SR04_Sensor_1.VCC, Part6.VIN, Part7.VCC, S1.3, S2.3, S3.3, S4.3, S5.3, S6.3, S7.3, S8.3, S9.3, S10.3, S11.3, S12.3
  N1: U2.GPIO36, R9.Pin_0, R11.Pin_0
  N2: U2.GPIO39, R6.Pin_1, S7.1
  N3: U2.GPIO34, R5.Pin_1, S6.1
  N4: U2.GPIO35, R3.Pin_1, S5.1
  N5: U2.GPIO32, R2.Pin_1, S4.1
  N6: U2.GPIO33, R4.Pin_1, S3.1
  N7: U2.GPIO25, R1.Pin_1, S2.1
  N8: U2.GPIO26, J1.pin2
  N9: U2.GPIO27, R8.Pin_1, S1.1
  N10: U2.GPIO14, R12.Pin_1, S9.1
  N11: U2.GPIO12, S10.1, R13.Pin_1
  GND: U2.GND, X5.GND, X6.GND, Part1.GND, Part2.GND, Part3.GND, TP1.pin6, SERVO1.GND, SERVO5.GND, SERVO6.GND, SERVO7.GND, SERVO8.GND, SERVO9.GND, SERVO10.GND, SERVO11.GND, SERVO12.GND, SERVO13.GND, SERVO14.GND, SERVO15.GND, SERVO16.GND, SERVO17.GND, SERVO18.GND, SERVO19.GND, SERVO20.GND, SERVO21.GND, SERVO22.GND, SERVO23.GND, SERVO24.GND, SERVO25.GND, SERVO26.GND, SERVO27.GND, SERVO28.GND, Part5.GND, SERVO29.GND, SERVO30.GND, SERVO31.GND, SERVO32.GND, SERVO33.GND, SERVO34.GND, SERVO35.GND, SERVO36.GND, HC-SR04_Sensor_1.GND, Part6.GND, Part7.GND, ESP32_-_Back1.GND#7, ESP32_-_Back2.GND#7, Part8.GND, Part9.GND, R1.Pin_0, R2.Pin_0, R3.Pin_0, R4.Pin_0, R5.Pin_0, R6.Pin_0, R7.Pin_0, R8.Pin_0, R11.Pin_1, J1.pin1, R12.Pin_0, R13.Pin_0, R14.Pin_0, R15.Pin_0
  N12: U2.GPIO13, S11.1, R14.Pin_1
  N13: U2.GPIO9, S12.1, R15.Pin_1
  N14: U2.GPIO10, HC-SR04_Sensor_1.ECHO
  N15: U2.GPIO11, HC-SR04_Sensor_1.TRIG
  +5V: U2.VIN, X5.+V, X6.+V, Part1.V+, Part2.V+, Part3.V+, SERVO1.+5V, SERVO5.+5V, SERVO6.+5V, SERVO7.+5V, SERVO8.+5V, SERVO9.+5V, SERVO10.+5V, SERVO11.+5V, SERVO12.+5V, SERVO13.+5V, SERVO14.+5V, SERVO15.+5V, SERVO16.+5V, SERVO17.+5V, SERVO18.+5V, SERVO19.+5V, SERVO20.+5V, SERVO21.+5V, SERVO22.+5V, SERVO23.+5V, SERVO24.+5V, SERVO25.+5V, SERVO26.+5V, SERVO27.+5V, SERVO28.+5V, Part5.V+, SERVO29.+5V, SERVO30.+5V, SERVO31.+5V, SERVO32.+5V, SERVO33.+5V, SERVO34.+5V, SERVO35.+5V, SERVO36.+5V, ESP32_-_Back1.5V, ESP32_-_Back2.5V, U3.O, R9.Pin_1
  N16: U2.GPIO6, X6.IN4
  N17: U2.GPIO7, X6.IN3
  N18: U2.GPIO8, X6.IN2
  N19: U2.GPIO15, X6.IN1
  N20: U2.GPIO2, R7.Pin_1, S8.1
  N21: U2.GPIO0, X5.IN4
  N22: U2.GPIO4, X5.IN3
  N23: U2.GPIO21, Part1.SDA, Part2.SDA, Part3.SDA, Part5.SDA, Part6.MOSI_SDA, Part7.SDA
  N24: U2.GPIO3, X5.IN2
  N25: U2.GPIO1, X5.IN1
  N26: U2.GPIO22, Part1.SCL, Part2.SCL, Part3.SCL, Part5.SCL, Part6.SCLK_SCK, Part7.SCL
  N27: MOTOR4.BLUE, X5.BLUE
  N28: MOTOR4.PINK, X5.PINK
  N29: MOTOR4.RED, X5.RED
  N30: MOTOR4.ORANGE, X5.ORANGE
  N31: MOTOR4.YELLOW, X5.YELLOW
  N32: MOTOR5.BLUE, X6.BLUE
  N33: MOTOR5.PINK, X6.PINK
  N34: MOTOR5.RED, X6.RED
  N35: MOTOR5.ORANGE, X6.ORANGE
  N36: MOTOR5.YELLOW, X6.YELLOW
  N37: Part1.OE, Part2.OE, Part3.OE, Part5.OE
  N38: Part1.13, SERVO30.Signal
  N39: Part1.14, SERVO29.Signal
  N40: Part1.15, SERVO1.Signal
  N41: Part2.0, SERVO5.Signal
  N42: Part2.1, SERVO6.Signal
  N43: Part2.2, SERVO7.Signal
  N44: Part2.4, SERVO8.Signal
  N45: Part2.5, SERVO9.Signal
  N46: Part2.6, SERVO10.Signal
  N47: Part2.8, SERVO11.Signal
  N48: Part2.9, SERVO12.Signal
  N49: Part2.10, SERVO13.Signal
  N50: Part2.12, SERVO14.Signal
  N51: Part2.13, SERVO15.Signal
  N52: Part2.14, SERVO16.Signal
  N53: Part3.1, SERVO17.Signal
  N54: Part3.2, SERVO18.Signal
  N55: Part3.3, SERVO19.Signal
  N56: Part3.5, SERVO23.Signal
  N57: Part3.6, SERVO24.Signal
  N58: Part3.7, SERVO21.Signal
  N59: Part3.9, SERVO25.Signal
  N60: Part3.10, SERVO26.Signal
  N61: Part3.11, SERVO20.Signal
  N62: Part3.13, SERVO27.Signal
  N63: Part3.14, SERVO28.Signal
  N64: Part3.15, SERVO22.Signal
  N65: TP1.pin1, D1.C
  N66: TP1.pin2, D1.A
  N67: TP1.pin3, U3.P
  N68: TP1.pin4, Part4.positive
  N69: TP1.pin5, Part4.negative
  N70: Part5.0, SERVO31.Signal
  N71: Part5.1, SERVO32.Signal
  N72: Part5.2, SERVO33.Signal
  N73: Part5.4, SERVO36.Signal
  N74: Part5.5, SERVO34.Signal
  N75: Part5.6, SERVO35.Signal
  N76: Part5.8, Part8.VDD
  N77: Part5.9, Part9.VDD

custom parts:
  ESP32-38PinWide: Generic 38-Pin ESP32 with wide format (only access to one side of pins on a breadboard) based on Stephen Lilley's HiLetgo ESP-WROOM-32 ESP32 ESP-32S Development Board.
  28BYJ-48 Stepper Motor: 28BYJ-48 gear-reduction stepper motor (small)
  X113647 Stepper Driver Board: A common stepper motor driver board based on ULN2003APG darlington array
  16-Channel 12-bit PCA9685 PWM/Servo Driver: The Adafruit 16-Channel 12-bit PWM/Servo Driver will drive up to 16 servos over I2C with only 2 pins. The on-board PCA9685 PWM controller will drive all 16 channels simultaneously with no additional processing overhead. What's more, you can chain up to 62 of them to control up to 992 servos - all with the same 2 pins
  TP4056: A DIP stand-in part for whatever IC you want. With 6 pins on a 300mil dual inline package (DIP) footprint.
  Lithium Ion Polymer Battery 3.7v 500mAh: Lithium ion polymer (also known as 'lipo' or 'lipoly') batteries are thin, light and powerful. The output ranges from 4.2V when completely charged to 3.7V. This battery has a capacity of 500mAh for a total of about 1.9 Wh. The batteries come pre-attached with a genuine 2-pin JST-PH connector as shown and include the necessary protection circuitry.
  Tower Pro SG90 servo: Original file by John De Cristofaro http://www.adafruit.com/products/1449 Adafruit Feedback Servo (Small) Edited by: e-radionica.com 28/9/2015
  OLED Monochrome 128x64 0.96 inch: These displays are small, only about 1" diameter, but very readable due to the high contrast of an OLED display. This display is made of 128x64 individual white OLED pixels, each one is turned on or off by the controller chip. Because the display makes its own light, no backlight is required. This reduces the power required to run the OLED and is why the display has such high contrast; we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
  ESP32 - CAM: The ESP32-CAM has a very competitive small-size camera module that can operate independently as a minimum system with a footprint of only 27*40.5*4.5mm and a deep sleep current of up to 6mA.
  NeoPixel Jewel: We fit seven of our tiny 5050 (5mm x 5mm) smart RGB LEDs onto a beautiful, round PCB with mounting holes and a chainable design to create what we think is our most elegant (and evening-wear appropriate) NeoPixel board yet. Use only one microcontroller pin to control as many as you can chain together! Each LED is addressable as the driver chip is inside the LED. Each one has ~18mA constant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
  Waveshare 2.9" eInk Display Breakout: This is an E-Ink display module, 2.9inch, 296x128 resolution, with embedded controller, communicating via SPI interface, supports partial refresh. Due to the advantages like ultra low power consumption, wide viewing angle, clear display without electricity, it is an ideal choice for applications such as shelf label, industrial instrument, and so on. Features No backlight, keeps displaying last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
